// Logisim project mainCPU.circ as structural Verilog: 1 circuit, main circuit main
module main (
  input  [7:0] in_1,
  input  in_2,
  input  in_3,
  input  in_4,
  input  [7:0] in_5,
  input  [7:0] in_6,
  input  [1:0] in_7,
  output [7:0] out_8,
  output [7:0] out_9,
  output [7:0] out_10
);

  wire and_1_out, and_2_out, clock_1_out, not_1_out, or_1_out, xor_1_out;
  wire [7:0] demultiplexer_1_out1, demultiplexer_1_out3, multiplexer_1_out, multiplexer_3_out;

  Demultiplexer #(.select(3), .width(8)) demultiplexer_1 (
    .out1(demultiplexer_1_out1), .out3(demultiplexer_1_out3), .in(in_1), .sel({in_4, in_3, in_2}));  // open: out0, out2, out4, out5, out6, out7, en
  Demultiplexer #(.select(3), .width(8)) demultiplexer_2 (
    .out1(out_8), .out2(out_9), .out3(out_10), .in(in_5), .sel({in_4, in_3, in_2}));  // open: out0, out4, out5, out6, out7, en
  Multiplexer #(.width(8)) multiplexer_1 (
    .in0(demultiplexer_1_out1), .in1(demultiplexer_1_out3), .out(multiplexer_1_out), .sel(in_4));  // open: en
  Multiplexer #(.select(2), .width(8)) multiplexer_2 (
    .in1(out_8), .in2(out_9), .in3(out_10));  // open: in0, out, sel, en
  not not_1 (not_1_out, in_4);
  or or_1 (or_1_out, in_2, in_3);
  xor xor_1 (xor_1_out, in_2, in_3);
  ROM rom_1 (.addr(multiplexer_1_out));  // open: data, sel
  Multiplexer #(.width(8)) multiplexer_3 (.out(multiplexer_3_out));  // open: in0, in1, sel, en
  and and_1 (and_1_out, not_1_out, or_1_out);
  and and_2 (and_2_out, in_4, xor_1_out);
  Clock clock_1 (.out(clock_1_out));
  RAM #(.bus("separate")) ram_1 (
    .addr(multiplexer_3_out), .str(and_1_out), .clk(clock_1_out), .ld(and_2_out));  // open: din, data, sel, clr
endmodule
